// Logisim project main.circ as structural Verilog: 1 circuit, main circuit Game
module Game (
);

  wire and_1_out, and_2_out, button_1_out, button_2_out, button_3_out, button_4_out, button_5_out,
       button_6_out, button_register_2_clock_2, button_register_2_r___w_selector_2, button_register_2_zero,
       button_register_3_clock_2, button_register_3_r___w_selector_2, button_register_3_zero,
       button_register_4_clock_2, button_register_4_r___w_selector_2, button_register_5_clock_2,
       button_register_5_r___w_selector_2, button_register_6_clock_2, button_register_6_r___w_selector_2,
       button_register_7_clock_2, button_register_7_r___w_selector_2, button_register_8_clock_2,
       button_register_8_r___w_selector_2, button_register_9_clock_2, button_register_9_r___w_selector_2,
       button_register_10_clock_2, button_register_10_r___w_selector_2, button_register_11_clock_2,
       button_register_11_r___w_selector_2, button_register_12_clock_2, button_register_12_r___w_selector_2,
       button_register_13_clock_2, button_register_13_r___w_selector_2, button_register_14_clock_2,
       button_register_14_r___w_selector_2, C, cdm_8_mark5_1_p2, cdm_8_mark5_1_p3, Clock, comparator_2_eq,
       Computer, D, Data, decoder_2_out0, decoder_2_out1, Gamemaster, Gamepad, H, Init, Instructions,
       not_1_out, not_2_out, Player, R___W_Selector;
  wire [1:0] Active_Bank, register_1_q;
  wire [3:0] button_driver_2_address_2, button_driver_3_address_2, button_driver_4_address_2,
       button_driver_5_address_2, button_driver_6_address_2, button_register_1_tens, button_register_1_units,
       button_register_2_address_2, button_register_2_driver, button_register_2_position___1,
       button_register_2_tens, button_register_2_units, button_register_3_address_2,
       button_register_3_position___1, button_register_3_tens, button_register_3_units,
       button_register_4_address_2, button_register_4_driver, button_register_4_position___1,
       button_register_4_tens, button_register_4_units, button_register_5_address_2,
       button_register_5_position___1, button_register_5_tens, button_register_5_units,
       button_register_6_address_2, button_register_6_driver, button_register_6_position___1,
       button_register_6_tens, button_register_6_units, button_register_7_address_2,
       button_register_7_position___1, button_register_7_tens, button_register_7_units,
       button_register_8_address_2, button_register_8_driver, button_register_8_position___1,
       button_register_8_tens, button_register_8_units, button_register_9_address_2,
       button_register_9_position___1, button_register_9_tens, button_register_9_units,
       button_register_10_address_2, button_register_10_driver, button_register_10_position___1,
       button_register_10_tens, button_register_10_units, button_register_11_address_2,
       button_register_11_position___1, button_register_11_tens, button_register_11_units,
       button_register_12_address_2, button_register_12_driver, button_register_12_position___1,
       button_register_12_tens, button_register_12_units, button_register_13_address_2,
       button_register_13_position___1, button_register_13_tens, button_register_13_units,
       button_register_14_address_2, button_register_14_position___1, button_register_14_tens,
       button_register_14_units, G_Address, increment_4_bits_1_out_2;
  wire [7:0] Address_Bus, button_register_1_dataout, button_register_2_dataout, button_register_3_dataout,
       button_register_4_dataout, button_register_5_dataout, button_register_6_dataout,
       button_register_7_dataout, button_register_8_dataout, button_register_9_dataout,
       button_register_10_dataout, button_register_11_dataout, button_register_12_dataout,
       button_register_13_dataout, button_register_14_dataout, cdm_8_mark5_1_p6, cdm_8_mark5_1_p7, Data_Bus,
       G_In;

  Clock clock_1 (.out(Clock));
  BitSelector #(.group(4)) bitselector_1 (.in(Address_Bus), .out(G_Address), .sel(1'b0));
  // CdM_8_mark5 cdm_8_mark5_1: pin names not known; wires that end beside it: Clock, cdm_8_mark5_1_p2, cdm_8_mark5_1_p3, R___W_Selector, Address_Bus, cdm_8_mark5_1_p6, cdm_8_mark5_1_p7
  Comparator #(.mode("unsigned")) comparator_1 (.a(Address_Bus), .b(8'hf0), .gt(Gamepad));  // open: eq, lt
  Decoder #(.disabled(0)) decoder_1 (.out0(Instructions), .out1(Data), .sel(cdm_8_mark5_1_p2), .en(cdm_8_mark5_1_p3));
  assign Data_Bus = not_1_out ? cdm_8_mark5_1_p6 : 8'bz;  // Controlled_Buffer controlled_buffer_1
  not not_1 (not_1_out, R___W_Selector);
  assign cdm_8_mark5_1_p7 = R___W_Selector ? Data_Bus : 8'bz;  // Controlled_Buffer controlled_buffer_2
  ROM rom_1 (.addr(Address_Bus), .data(Data_Bus), .sel(Init));
  ROM rom_2 (.addr(Address_Bus), .data(Data_Bus), .sel(Gamemaster));
  ROM rom_3 (.addr(Address_Bus), .data(Data_Bus), .sel(Player));
  ROM rom_4 (.addr(Address_Bus), .data(Data_Bus), .sel(Computer));
  assign G_In = decoder_2_out0 ? Data_Bus : 8'bz;  // Controlled_Buffer controlled_buffer_3
  assign Data_Bus = decoder_2_out1 ? button_register_1_dataout : 8'bz;  // Controlled_Buffer controlled_buffer_4
  Comparator #(.mode("unsigned")) comparator_2 (.a(Address_Bus), .b(8'he0), .eq(comparator_2_eq));  // open: gt, lt
  Decoder #(.disabled(0)) decoder_2 (.out0(decoder_2_out0), .out1(decoder_2_out1), .sel(R___W_Selector), .en(Gamepad));
  LED led_1 (.in(C));
  LED led_2 (.in(C));
  LED led_3 (.in(C));
  Pull_Resistor pull_resistor_1 (.node(C));
  not not_2 (not_2_out, Gamepad);
  Decoder #(.select(2), .disabled(0)) decoder_3 (
    .out0(Init), .out1(Gamemaster), .out2(Player), .out3(Computer), .sel(register_1_q), .en(not_2_out));
  Register #(.width(2)) register_1 (.D(Active_Bank), .en(Clock), .Q(register_1_q), .clk(and_1_out));  // open: clr
  and and_1 (and_1_out, Data, comparator_2_eq);
  Hex_Digit_Display hex_digit_display_1 (.value(button_register_1_tens));  // open: dp
  Hex_Digit_Display hex_digit_display_2 (.value(button_register_1_units));  // open: dp
  Button_Register button_register_1 (
    .Data(button_register_3_dataout), .Position(button_register_3_position___1),
    .Address(button_register_3_address_2), .Clock(button_register_3_clock_2),
    .R___W_Selector(button_register_3_r___w_selector_2), .Dataout(button_register_1_dataout),
    .Tens(button_register_1_tens), .Units(button_register_1_units));  // open: Position___1, Address_2, Driver, Clock_2, R___W_Selector_2, Zero
  Win_Lose_Draw win_lose_draw_1 (
    .out_5(C), .Tens(button_register_1_tens), .Units(button_register_1_units), .out_6(H),
    .Is_Zero(button_register_3_zero), .Another(D));
  Hex_Digit_Display hex_digit_display_3 (.value(button_register_3_tens));  // open: dp
  Hex_Digit_Display hex_digit_display_4 (.value(button_register_2_tens));  // open: dp
  Button_Register button_register_2 (
    .Data(G_In), .Position(4'b0000), .Address(G_Address), .Clock(Clock), .R___W_Selector(and_2_out),
    .Dataout(button_register_2_dataout), .Position___1(button_register_2_position___1),
    .Address_2(button_register_2_address_2), .Driver(button_register_2_driver),
    .Clock_2(button_register_2_clock_2), .R___W_Selector_2(button_register_2_r___w_selector_2),
    .Zero(button_register_2_zero), .Tens(button_register_2_tens), .Units(button_register_2_units));
  Button_Driver button_driver_1 (
    .Position(button_register_2_driver), .Address(button_driver_2_address_2), .Button(button_1_out));  // open: Address_2, Trigger
  Button button_1 (.out(button_1_out));
  and and_2 (and_2_out, Data, ~R___W_Selector, Gamepad);  // AND_Gate
  Button_Register button_register_3 (
    .Data(button_register_5_dataout), .Position(button_register_5_position___1),
    .Address(button_register_5_address_2), .Clock(button_register_5_clock_2),
    .R___W_Selector(button_register_5_r___w_selector_2), .Dataout(button_register_3_dataout),
    .Position___1(button_register_3_position___1), .Address_2(button_register_3_address_2),
    .Clock_2(button_register_3_clock_2), .R___W_Selector_2(button_register_3_r___w_selector_2),
    .Zero(button_register_3_zero), .Tens(button_register_3_tens), .Units(button_register_3_units));  // open: Driver
  Hex_Digit_Display hex_digit_display_5 (.value(button_register_5_tens));  // open: dp
  Hex_Digit_Display hex_digit_display_6 (.value(button_register_3_units));  // open: dp
  Hex_Digit_Display hex_digit_display_7 (.value(button_register_2_units));  // open: dp
  Hex_Digit_Display hex_digit_display_8 (.value(button_register_4_tens));  // open: dp
  Button_Register button_register_4 (
    .Data(button_register_2_dataout), .Position(button_register_2_position___1),
    .Address(button_register_2_address_2), .Clock(button_register_2_clock_2),
    .R___W_Selector(button_register_2_r___w_selector_2), .Dataout(button_register_4_dataout),
    .Position___1(button_register_4_position___1), .Address_2(button_register_4_address_2),
    .Driver(button_register_4_driver), .Clock_2(button_register_4_clock_2),
    .R___W_Selector_2(button_register_4_r___w_selector_2), .Zero(button_register_2_zero),
    .Tens(button_register_4_tens), .Units(button_register_4_units));
  Button_Driver button_driver_2 (
    .Position(button_register_4_driver), .Address_2(button_driver_2_address_2),
    .Address(button_driver_3_address_2), .Button(button_2_out));  // open: Trigger
  Button_Register button_register_5 (
    .Data(button_register_7_dataout), .Position(button_register_7_position___1),
    .Address(button_register_7_address_2), .Clock(button_register_7_clock_2),
    .R___W_Selector(button_register_7_r___w_selector_2), .Dataout(button_register_5_dataout),
    .Position___1(button_register_5_position___1), .Address_2(button_register_5_address_2),
    .Clock_2(button_register_5_clock_2), .R___W_Selector_2(button_register_5_r___w_selector_2),
    .Zero(button_register_3_zero), .Tens(button_register_5_tens), .Units(button_register_5_units));  // open: Driver
  Hex_Digit_Display hex_digit_display_9 (.value(button_register_5_units));  // open: dp
  Hex_Digit_Display hex_digit_display_10 (.value(button_register_4_units));  // open: dp
  Button_Register button_register_6 (
    .Data(button_register_4_dataout), .Position(button_register_4_position___1),
    .Address(button_register_4_address_2), .Clock(button_register_4_clock_2),
    .R___W_Selector(button_register_4_r___w_selector_2), .Dataout(button_register_6_dataout),
    .Position___1(button_register_6_position___1), .Address_2(button_register_6_address_2),
    .Driver(button_register_6_driver), .Clock_2(button_register_6_clock_2),
    .R___W_Selector_2(button_register_6_r___w_selector_2), .Zero(button_register_2_zero),
    .Tens(button_register_6_tens), .Units(button_register_6_units));
  Button_Driver button_driver_3 (
    .Position(button_register_6_driver), .Address_2(button_driver_3_address_2),
    .Address(button_driver_4_address_2), .Button(button_3_out));  // open: Trigger
  Button button_2 (.out(button_2_out));
  Hex_Digit_Display hex_digit_display_11 (.value(button_register_7_units));  // open: dp
  Hex_Digit_Display hex_digit_display_12 (.value(button_register_7_tens));  // open: dp
  Hex_Digit_Display hex_digit_display_13 (.value(button_register_6_units));  // open: dp
  Hex_Digit_Display hex_digit_display_14 (.value(button_register_6_tens));  // open: dp
  Button button_3 (.out(button_3_out));
  Button_Register button_register_7 (
    .Data(button_register_9_dataout), .Position(button_register_9_position___1),
    .Address(button_register_9_address_2), .Clock(button_register_9_clock_2),
    .R___W_Selector(button_register_9_r___w_selector_2), .Dataout(button_register_7_dataout),
    .Position___1(button_register_7_position___1), .Address_2(button_register_7_address_2),
    .Clock_2(button_register_7_clock_2), .R___W_Selector_2(button_register_7_r___w_selector_2),
    .Zero(button_register_3_zero), .Tens(button_register_7_tens), .Units(button_register_7_units));  // open: Driver
  Hex_Digit_Display hex_digit_display_15 (.value(button_register_9_tens));  // open: dp
  Hex_Digit_Display hex_digit_display_16 (.value(button_register_8_tens));  // open: dp
  Button_Register button_register_8 (
    .Data(button_register_6_dataout), .Position(button_register_6_position___1),
    .Address(button_register_6_address_2), .Clock(button_register_6_clock_2),
    .R___W_Selector(button_register_6_r___w_selector_2), .Dataout(button_register_8_dataout),
    .Position___1(button_register_8_position___1), .Address_2(button_register_8_address_2),
    .Driver(button_register_8_driver), .Clock_2(button_register_8_clock_2),
    .R___W_Selector_2(button_register_8_r___w_selector_2), .Zero(button_register_2_zero),
    .Tens(button_register_8_tens), .Units(button_register_8_units));
  Button_Driver button_driver_4 (
    .Position(button_register_8_driver), .Address_2(button_driver_4_address_2),
    .Address(button_driver_5_address_2), .Button(button_4_out));  // open: Trigger
  Button button_4 (.out(button_4_out));
  Button_Register button_register_9 (
    .Data(button_register_11_dataout), .Position(button_register_11_position___1),
    .Address(button_register_11_address_2), .Clock(button_register_11_clock_2),
    .R___W_Selector(button_register_11_r___w_selector_2), .Dataout(button_register_9_dataout),
    .Position___1(button_register_9_position___1), .Address_2(button_register_9_address_2),
    .Clock_2(button_register_9_clock_2), .R___W_Selector_2(button_register_9_r___w_selector_2),
    .Zero(button_register_3_zero), .Tens(button_register_9_tens), .Units(button_register_9_units));  // open: Driver
  Hex_Digit_Display hex_digit_display_17 (.value(button_register_9_units));  // open: dp
  Hex_Digit_Display hex_digit_display_18 (.value(button_register_8_units));  // open: dp
  Button_Register button_register_10 (
    .Data(button_register_8_dataout), .Position(button_register_8_position___1),
    .Address(button_register_8_address_2), .Clock(button_register_8_clock_2),
    .R___W_Selector(button_register_8_r___w_selector_2), .Dataout(button_register_10_dataout),
    .Position___1(button_register_10_position___1), .Address_2(button_register_10_address_2),
    .Driver(button_register_10_driver), .Clock_2(button_register_10_clock_2),
    .R___W_Selector_2(button_register_10_r___w_selector_2), .Zero(button_register_2_zero),
    .Tens(button_register_10_tens), .Units(button_register_10_units));
  Button_Driver button_driver_5 (
    .Position(button_register_10_driver), .Address_2(button_driver_5_address_2),
    .Address(button_driver_6_address_2), .Button(button_5_out));  // open: Trigger
  Hex_Digit_Display hex_digit_display_19 (.value(button_register_11_units));  // open: dp
  Hex_Digit_Display hex_digit_display_20 (.value(button_register_11_tens));  // open: dp
  Hex_Digit_Display hex_digit_display_21 (.value(button_register_10_tens));  // open: dp
  Hex_Digit_Display hex_digit_display_22 (.value(button_register_10_units));  // open: dp
  Button button_5 (.out(button_5_out));
  Button_Register button_register_11 (
    .Data(button_register_13_dataout), .Position(button_register_13_position___1),
    .Address(button_register_13_address_2), .Clock(button_register_13_clock_2),
    .R___W_Selector(button_register_13_r___w_selector_2), .Dataout(button_register_11_dataout),
    .Position___1(button_register_11_position___1), .Address_2(button_register_11_address_2),
    .Clock_2(button_register_11_clock_2), .R___W_Selector_2(button_register_11_r___w_selector_2),
    .Zero(button_register_3_zero), .Tens(button_register_11_tens), .Units(button_register_11_units));  // open: Driver
  Hex_Digit_Display hex_digit_display_23 (.value(button_register_13_tens));  // open: dp
  Hex_Digit_Display hex_digit_display_24 (.value(button_register_13_units));  // open: dp
  Hex_Digit_Display hex_digit_display_25 (.value(button_register_12_units));  // open: dp
  Hex_Digit_Display hex_digit_display_26 (.value(button_register_12_tens));  // open: dp
  Button_Register button_register_12 (
    .Data(button_register_10_dataout), .Position(button_register_10_position___1),
    .Address(button_register_10_address_2), .Clock(button_register_10_clock_2),
    .R___W_Selector(button_register_10_r___w_selector_2), .Dataout(button_register_12_dataout),
    .Position___1(button_register_12_position___1), .Address_2(button_register_12_address_2),
    .Driver(button_register_12_driver), .Clock_2(button_register_12_clock_2),
    .R___W_Selector_2(button_register_12_r___w_selector_2), .Zero(button_register_2_zero),
    .Tens(button_register_12_tens), .Units(button_register_12_units));
  Button_Driver button_driver_6 (
    .Position(button_register_12_driver), .Address_2(button_driver_6_address_2), .Button(button_6_out));  // open: Address, Trigger
  Button button_6 (.out(button_6_out));
  Button_Register button_register_13 (
    .Data(button_register_14_dataout), .Position(increment_4_bits_1_out_2),
    .Address(button_register_14_address_2), .Clock(button_register_14_clock_2),
    .R___W_Selector(button_register_14_r___w_selector_2), .Dataout(button_register_13_dataout),
    .Position___1(button_register_13_position___1), .Address_2(button_register_13_address_2),
    .Clock_2(button_register_13_clock_2), .R___W_Selector_2(button_register_13_r___w_selector_2),
    .Zero(button_register_3_zero), .Tens(button_register_13_tens), .Units(button_register_13_units));  // open: Driver
  Pull_Resistor #(.pull(1)) pull_resistor_2 (.node(button_register_3_zero));
  Win_Lose_Draw win_lose_draw_2 (
    .out_5(D), .Tens(button_register_14_tens), .Units(button_register_14_units), .out_6(H),
    .Is_Zero(button_register_2_zero), .Another(C));
  Pull_Resistor #(.pull(1)) pull_resistor_3 (.node(button_register_2_zero));
  Hex_Digit_Display hex_digit_display_27 (.value(button_register_14_tens));  // open: dp
  Button_Register button_register_14 (
    .Data(button_register_12_dataout), .Position(button_register_12_position___1),
    .Address(button_register_12_address_2), .Clock(button_register_12_clock_2),
    .R___W_Selector(button_register_12_r___w_selector_2), .Dataout(button_register_14_dataout),
    .Position___1(button_register_14_position___1), .Address_2(button_register_14_address_2),
    .Clock_2(button_register_14_clock_2), .R___W_Selector_2(button_register_14_r___w_selector_2),
    .Tens(button_register_14_tens), .Units(button_register_14_units));  // open: Driver, Zero
  Increment__4_bits increment_4_bits_1 (.in_1(button_register_14_position___1), .out_2(increment_4_bits_1_out_2));
  LED led_4 (.in(H));
  LED led_5 (.in(H));
  Pull_Resistor pull_resistor_4 (.node(H));
  LED led_6 (.in(H));
  Hex_Digit_Display hex_digit_display_28 (.value(button_register_14_units));  // open: dp

  // Other names for the same wires on the sheet: G_Data[7:0] = Data_Bus

  // Notes on the sheet:
  //   contents of rom_1 (hex, n*v repeats v):
  //   d2 4 d3 0 d0 f1 d1 f7 74 ed f a2 8c ee 8 a3 d0 f9 d1 ff 74 ed 1b a2 8c ee 14 a3 d0 ef d1 2 a1
endmodule
